# Fritzing sketch MAIDS FINAL CIRCUITD DESIGN 12-10-2019 (saved by Fritzing 0.9.3b)
circuit board: 6.6cm x 5.6cm
breadboards: 1

parts:
  ARM_SW = Pushbutton [package="[THT]"]
  MOTSENS = HC-SR501 Body Sensor Module
  J1 = female pin header, 3 pins [form="♀ (female)"]
  SNDSENS = Breakout Board for Electret Microphone
  J2 = female pin header, 3 pins [form="♀ (female)"]
  BUZZER = Piezo Speaker
  LED1 = DUO LED RG [package="5 mm [THT]"]
  J6 = female pin header, 2 pins [form="♀ (female)"]
  J7 = female pin header, 3 pins [form="♀ (female)"]
  Raspberry_Pi_1 = Raspberry Pi 3 [part_number=RPI-3-V1.2]

nets:
  VCC: ARM_SW.Pin_1, ARM_SW.Pin_2, MOTSENS.VCC, J1.pin3, SNDSENS.VCC, J2.pin1, Raspberry_Pi_1.GPIO4, Raspberry_Pi_1.5V
  N1: ARM_SW.Pin_3, ARM_SW.Pin_4
  N2: MOTSENS.OUT, J1.pin2, Raspberry_Pi_1.GPIO5
  GND: MOTSENS.GND, J1.pin1, SNDSENS.GND, J2.pin2, BUZZER.pin1, LED1.common_cathode, J6.pin1, J7.pin2, Raspberry_Pi_1.GND
  N3: SNDSENS.AUD, J2.pin3, Raspberry_Pi_1.GPIO6
  N4: BUZZER.pin2, J6.pin2, Raspberry_Pi_1.GPIO13
  N5: LED1.red_anode, J7.pin1, Raspberry_Pi_1.GPIO27
  N6: LED1.green_anode, J7.pin3, Raspberry_Pi_1.GPIO22

notes:
  C. MEIS- N00674230- MAIDS
  MAIDS PROJECT  BREADBOARD DESIGN
  CENG317 - HUMBER COLLEGE 2019
  MAIDS PROJECT FINAL
  MOTS GPIO5
  SNDS GPIO6
  BUZ GPIO13
  GLED GPIO22
  RLED GPIO27
  FOR MY SON, CONOR!

custom parts:
  HC-SR501 Body Sensor Module: Pyroelectric Infrared PIR Motion Sensor Detector Module
